// Logisim project encoderReader.circ as structural Verilog: 3 circuits, main circuit reader
module reader (
  input  A,
  input  B,
  output Emoins,
  output Eplus
);

  wire d_ff_1_q, not_1_out;

  D_Flip_Flop d_ff_1 (.D(not_1_out), .clk(A), .Q(d_ff_1_q));  // open: Qn, preset, reset
  not not_1 (not_1_out, B);
  and and_1 (Emoins, ~d_ff_1_q, B);  // AND_Gate
  and and_2 (Eplus, d_ff_1_q, B);
endmodule

module antiRebond (
  input  dataIn,
  output o
);

  wire and_1_out, and_2_out, and_3_out, and_4_out, clock_1_out, d_ff_1_q, d_ff_2_q, d_ff_3_q, d_ff_4_q;

  Clock clock_1 (.out(clock_1_out));
  D_Flip_Flop d_ff_1 (.D(dataIn), .clk(clock_1_out), .Q(d_ff_1_q));  // open: Qn, preset, reset
  D_Flip_Flop d_ff_2 (.D(d_ff_1_q), .clk(clock_1_out), .Q(d_ff_2_q));  // open: Qn, preset, reset
  D_Flip_Flop d_ff_3 (.D(d_ff_2_q), .clk(clock_1_out), .Q(d_ff_3_q));  // open: Qn, preset, reset
  D_Flip_Flop d_ff_4 (.D(d_ff_3_q), .clk(clock_1_out), .Q(d_ff_4_q));  // open: Qn, preset, reset
  and and_1 (and_1_out, d_ff_3_q, d_ff_4_q);
  and and_2 (and_2_out, d_ff_2_q, d_ff_4_q);
  and and_3 (and_3_out, d_ff_1_q, d_ff_4_q);
  and and_4 (and_4_out, d_ff_1_q, d_ff_2_q, d_ff_3_q);
  or or_1 (o, and_1_out, and_2_out, and_3_out, and_4_out);
endmodule

module main (
  input  in_1,
  input  in_2,
  output direction,
  output impulsion
);

  wire antirebond_1_o, antirebond_2_o;

  antiRebond antirebond_1 (.dataIn(in_1), .o(antirebond_1_o));
  antiRebond antirebond_2 (.dataIn(in_2), .o(antirebond_2_o));
  reader reader_1 (.A(antirebond_1_o), .B(antirebond_2_o), .Emoins(direction), .Eplus(impulsion));
endmodule
