// Logisim project main_circuit.circ as structural Verilog: 12 circuits, main circuit main
module main (
  input  Enable,
  input  R,
  output [7:0] S0,
  output [7:0] S1,
  output [7:0] S2,
  output [7:0] S3,
  output [7:0] S4,
  output [7:0] S5
);

  wire [6:0] t_h, t_m, t_s;

  _7_Segment_Display u_7_segment_display_1 (
    .g(S5[6]), .f(S5[5]), .a(S5[0]), .b(S5[1]), .e(S5[4]), .d(S5[3]), .c(S5[2]), .dp(S5[7]));
  _7_Segment_Display u_7_segment_display_2 (
    .g(S4[6]), .f(S4[5]), .a(S4[0]), .b(S4[1]), .e(S4[4]), .d(S4[3]), .c(S4[2]), .dp(S4[7]));
  timer t (.Enable(Enable), .R(R), .S(t_s), .M(t_m), .H(t_h));
  _7_Segment_Display u_7_segment_display_3 (
    .g(S3[6]), .f(S3[5]), .a(S3[0]), .b(S3[1]), .e(S3[4]), .d(S3[3]), .c(S3[2]), .dp(S3[7]));
  print_hour ph_gangbang (.S(t_s), .M(t_m), .H(t_h), .S0(S0), .S1(S1), .S2(S2), .S3(S3), .S4(S4), .S5(S5));
  _7_Segment_Display u_7_segment_display_4 (
    .g(S2[6]), .f(S2[5]), .a(S2[0]), .b(S2[1]), .e(S2[4]), .d(S2[3]), .c(S2[2]), .dp(S2[7]));
  _7_Segment_Display u_7_segment_display_5 (
    .g(S1[6]), .f(S1[5]), .a(S1[0]), .b(S1[1]), .e(S1[4]), .d(S1[3]), .c(S1[2]));  // open: dp
  _7_Segment_Display u_7_segment_display_6 (
    .g(S0[6]), .f(S0[5]), .a(S0[0]), .b(S0[1]), .e(S0[4]), .d(S0[3]), .c(S0[2]));  // open: dp
endmodule

module base24Increment (
  input  Enable,
  input  Clk,
  input  RESET,
  output Q0,
  output Q1,
  output Q2,
  output Q3,
  output [4:0] S,
  output Q4,
  output Overflow
);

  wire and_1_out, and_2_out, d_ff_1_q, t_ff_1_qn, t_ff_2_qn, t_ff_3_qn, t_ff_4_qn;

  T_Flip_Flop t_ff_1 (.T(Enable), .clk(Clk), .Q(Q0), .Qn(t_ff_1_qn), .reset(Overflow));  // open: preset
  T_Flip_Flop t_ff_2 (.T(Enable), .clk(t_ff_1_qn), .Q(Q1), .Qn(t_ff_2_qn), .reset(Overflow));  // open: preset
  T_Flip_Flop t_ff_3 (.T(Enable), .clk(t_ff_2_qn), .Q(Q2), .Qn(t_ff_3_qn), .reset(Overflow));  // open: preset
  T_Flip_Flop t_ff_4 (.T(Enable), .clk(t_ff_3_qn), .Q(Q3), .Qn(t_ff_4_qn), .reset(Overflow));  // open: preset
  T_Flip_Flop t_ff_5 (.T(Enable), .clk(t_ff_4_qn), .Q(Q4), .reset(Overflow));  // open: Qn, preset
  or or_1 (Overflow, and_2_out, d_ff_1_q);
  D_Flip_Flop d_ff_1 (.D(1'b1), .clk(RESET), .Q(d_ff_1_q), .reset(and_1_out));  // open: Qn, preset
  and and_1 (and_1_out, Clk, d_ff_1_q);
  and and_2 (and_2_out, Q4, Q3);

  assign S = {Q4, Q3, Q2, Q1, Q0};

  // Notes on the sheet:
  //   RESET: pull=down
endmodule

module base60Increment (
  input  Enable,
  input  Clk,
  input  RESET,
  output Q0,
  output Q1,
  output Q2,
  output Q3,
  output [5:0] S,
  output Q4,
  output Q5,
  output Overflow
);

  wire and_1_out, and_2_out, d_ff_1_q, d_ff_2_q, nor_1_out, t_ff_1_qn, t_ff_2_qn, t_ff_3_qn, t_ff_4_qn,
       t_ff_5_qn;

  T_Flip_Flop t_ff_1 (.T(Enable), .clk(Clk), .Q(Q0), .Qn(t_ff_1_qn), .reset(Overflow));  // open: preset
  T_Flip_Flop t_ff_2 (.T(Enable), .clk(t_ff_1_qn), .Q(Q1), .Qn(t_ff_2_qn), .reset(Overflow));  // open: preset
  T_Flip_Flop t_ff_3 (.T(Enable), .clk(t_ff_2_qn), .Q(Q2), .Qn(t_ff_3_qn), .reset(Overflow));  // open: preset
  T_Flip_Flop t_ff_4 (.T(Enable), .clk(t_ff_3_qn), .Q(Q3), .Qn(t_ff_4_qn), .reset(Overflow));  // open: preset
  T_Flip_Flop t_ff_5 (.T(Enable), .clk(t_ff_4_qn), .Q(Q4), .Qn(t_ff_5_qn), .reset(Overflow));  // open: preset
  T_Flip_Flop t_ff_6 (.T(Enable), .clk(t_ff_5_qn), .Q(Q5), .reset(Overflow));  // open: Qn, preset
  or or_1 (Overflow, d_ff_2_q, d_ff_1_q);
  D_Flip_Flop d_ff_1 (.D(1'b1), .clk(RESET), .Q(d_ff_1_q), .reset(and_1_out));  // open: Qn, preset
  and and_1 (and_1_out, Clk, d_ff_1_q);
  and and_2 (and_2_out, Q5, Q4, Q3, Q2);
  nor nor_1 (nor_1_out, Q0, Q1, Q2, Q3, Q4, Q5, Q5);
  D_Flip_Flop d_ff_2 (.D(1'b1), .clk(and_2_out), .Q(d_ff_2_q), .reset(nor_1_out));  // open: Qn, preset

  assign S = {Q5, Q4, Q3, Q2, Q1, Q0};

  // Notes on the sheet:
  //   RESET: pull=down
endmodule

module timer (
  input  Enable,
  input  R,
  output [6:0] S,
  output [6:0] M,
  output [6:0] H
);

  wire b1_overflow, b2_overflow, clock_1_out;

  Clock clock_1 (.out(clock_1_out));
  base60Increment b1 (
    .Enable(Enable), .Clk(clock_1_out), .RESET(R), .Q0(S[0]), .Q1(S[1]), .Q2(S[2]), .Q3(S[3]), .Q4(S[4]),
    .Q5(S[5]), .Overflow(b1_overflow));  // open: S
  base60Increment b2 (
    .Enable(Enable), .Clk(b1_overflow), .RESET(R), .Q0(M[0]), .Q1(M[1]), .Q2(M[2]), .Q3(M[3]), .Q4(M[4]),
    .Q5(M[5]), .Overflow(b2_overflow));  // open: S
  base24Increment b3 (
    .Enable(Enable), .Clk(b2_overflow), .RESET(R), .Q0(H[0]), .Q1(H[1]), .Q2(H[2]), .Q3(H[3]), .Q4(H[4]));  // open: S, Overflow

  assign H[6:5] = 2'b00;
  assign M[6] = 1'b0;
  assign S[6] = 1'b0;
endmodule

module shifteur4 (
  input  [3:0] E,
  output [3:0] S
);


  assign S = {E[2:0], 1'b0};
endmodule

module shifteur7 (
  input  [6:0] E,
  output [6:0] S
);


  assign S = {E[5:0], 1'b0};
endmodule

module decodeur_7seg_mieux (
  input  P,
  input  [4:0] E,
  output [7:0] S
);

  wire and_1_out, and_2_out, and_3_out, and_4_out, and_5_out, and_6_out, and_7_out, and_8_out, and_9_out,
       and_10_out, and_11_out, and_12_out, and_13_out, and_14_out, and_15_out, and_16_out, and_17_out,
       and_18_out, and_19_out, and_20_out, and_21_out, and_22_out, and_23_out, and_24_out, and_25_out,
       and_26_out, and_27_out, and_28_out, and_29_out, and_30_out, and_31_out, and_32_out, and_33_out,
       and_34_out, and_35_out, and_36_out, and_37_out, and_38_out, and_39_out, and_40_out, and_41_out,
       and_42_out, and_43_out, and_44_out, and_45_out, and_46_out, and_47_out, and_48_out, and_49_out,
       and_50_out, and_51_out, and_52_out, and_53_out, and_54_out, and_55_out, and_56_out, and_57_out,
       and_58_out, and_59_out, and_60_out, not_1_out, not_2_out, not_3_out, not_4_out, not_5_out;

  not not_1 (not_1_out, E[4]);
  not not_2 (not_2_out, E[3]);
  not not_3 (not_3_out, E[2]);
  not not_4 (not_4_out, E[1]);
  not not_5 (not_5_out, E[0]);
  and and_1 (and_1_out, not_3_out, not_4_out, not_5_out);
  and and_2 (and_2_out, not_1_out, E[1], not_5_out);
  and and_3 (and_3_out, not_2_out, E[1], E[0]);
  and and_4 (and_4_out, not_2_out, E[2], E[0]);
  and and_5 (and_5_out, not_1_out, E[2], E[1]);
  and and_6 (and_6_out, not_1_out, E[3], not_5_out);
  and and_7 (and_7_out, E[3], not_3_out, not_4_out);
  and and_8 (and_8_out, E[4], E[3], not_3_out, E[0]);
  and and_9 (and_9_out, not_1_out, not_2_out, not_3_out);
  and and_10 (and_10_out, not_1_out, not_2_out, not_4_out, not_5_out);
  and and_11 (and_11_out, not_1_out, not_3_out, not_4_out);
  and and_12 (and_12_out, not_2_out, E[1], E[0]);
  and and_13 (and_13_out, E[3], not_3_out, not_5_out);
  and and_14 (and_14_out, not_1_out, E[3], not_4_out, E[0]);
  and and_15 (and_15_out, E[4], not_2_out, E[0]);
  and and_16 (and_16_out, E[4], E[3], not_3_out, E[1]);
  and and_17 (and_17_out, E[4], E[3], E[1], not_5_out);
  and and_18 (and_18_out, not_1_out, not_2_out, not_4_out);
  and and_19 (and_19_out, not_1_out, not_3_out, not_4_out);
  and and_20 (and_20_out, not_2_out, not_3_out, not_4_out);
  and and_21 (and_21_out, not_1_out, not_4_out, E[0]);
  and and_22 (and_22_out, not_2_out, E[0]);
  and and_23 (and_23_out, not_3_out, not_4_out, E[0]);
  and and_24 (and_24_out, not_2_out, E[2], E[1]);
  and and_25 (and_25_out, not_1_out, E[3], not_3_out);
  and and_26 (and_26_out, E[3], not_3_out, E[1], not_5_out);
  and and_27 (and_27_out, E[4], E[2], E[1], E[0]);
  and and_28 (and_28_out, not_2_out, not_3_out, not_4_out, not_5_out);
  and and_29 (and_29_out, not_1_out, not_2_out, E[1], not_5_out);
  and and_30 (and_30_out, not_3_out, E[1], E[0]);
  and and_31 (and_31_out, not_1_out, E[2], not_4_out, E[0]);
  and and_32 (and_32_out, not_1_out, E[3], not_4_out);
  and and_33 (and_33_out, E[3], not_4_out, E[0]);
  and and_34 (and_34_out, not_1_out, E[3], E[2], not_5_out);
  and and_35 (and_35_out, E[4], not_2_out, not_4_out, not_5_out);
  and and_36 (and_36_out, E[4], E[1], E[0]);
  and and_37 (and_37_out, E[4], E[3], not_3_out, E[1]);
  and and_38 (and_38_out, not_3_out, not_5_out);
  and and_39 (and_39_out, not_2_out, E[1], not_5_out);
  and and_40 (and_40_out, E[3], E[1], E[0]);
  and and_41 (and_41_out, not_1_out, E[3], E[2]);
  and and_42 (and_42_out, E[4], not_2_out);
  and and_43 (and_43_out, not_3_out, not_4_out, not_5_out);
  and and_44 (and_44_out, not_1_out, E[2], not_5_out);
  and and_45 (and_45_out, not_2_out, E[2], not_4_out);
  and and_46 (and_46_out, not_1_out, E[3], not_3_out);
  and and_47 (and_47_out, not_1_out, E[3], E[1]);
  and and_48 (and_48_out, E[3], E[1], not_5_out);
  and and_49 (and_49_out, E[4], not_3_out, not_4_out);
  and and_50 (and_50_out, E[4], not_3_out, not_5_out);
  and and_51 (and_51_out, E[4], not_2_out, E[2], E[0]);
  and and_52 (and_52_out, not_1_out, not_3_out, E[1]);
  and and_53 (and_53_out, not_1_out, not_2_out, E[2], not_4_out);
  and and_54 (and_54_out, not_2_out, E[2], E[1], not_5_out);
  and and_55 (and_55_out, not_1_out, E[3], not_3_out);
  and and_56 (and_56_out, E[3], not_3_out, E[0]);
  and and_57 (and_57_out, E[3], not_4_out, E[0]);
  and and_58 (and_58_out, not_1_out, E[3], E[1]);
  and and_59 (and_59_out, E[4], not_3_out, not_4_out);
  and and_60 (and_60_out, E[4], E[3], not_4_out);
  or or_1 (S[0], and_1_out, and_2_out, and_3_out, and_4_out, and_5_out, and_6_out, and_7_out, and_8_out);
  or or_2 (S[1], and_9_out, and_10_out, and_11_out, and_12_out, and_13_out, and_14_out, and_15_out, and_16_out, and_17_out);
  or or_3 (S[2], and_18_out, and_19_out, and_20_out, and_21_out, and_22_out, and_23_out, and_24_out, and_25_out, and_26_out, and_27_out);
  or or_4 (S[3], and_28_out, and_29_out, and_30_out, and_31_out, and_32_out, and_33_out, and_34_out, and_35_out, and_36_out, and_37_out);
  or or_5 (S[4], and_38_out, and_39_out, and_40_out, and_41_out, and_42_out);
  or or_6 (S[5], and_43_out, and_44_out, and_45_out, and_46_out, and_47_out, and_48_out, and_49_out, and_50_out, and_51_out);
  or or_7 (S[6], and_52_out, and_53_out, and_54_out, and_55_out, and_56_out, and_57_out, and_58_out, and_59_out, and_60_out);

  assign S[7] = P;

  // Notes on the sheet:
  //   Chiffres de 0a9 puis lettres de AaZ
  //   Enfin, -,=,smiley(pt1),smiley(pt2)
  //   Manque k,q,r,t,v,w,x,y
endmodule

module double_dabble_1step (
  input  [3:0] A0,
  input  [3:0] A1,
  input  [6:0] E,
  output [3:0] A0out,
  output [3:0] A1out,
  output [6:0] Eout
);

  wire [0:0] adder_3_cout, adder_3_out;
  wire [2:0] adder_3_out_2;
  wire [3:0] adder_1_out, adder_5_out, and_1_out, and_2_out, c1_s, c2_s, s1_s, s2_s;

  Adder #(.width(4)) adder_1 (.a({3'b000, adder_3_cout[0]}), .b(A1), .out(adder_1_out), .cin(1'b0));  // open: cout
  comparator5 c1 (.E(A0), .S(c1_s));
  shifteur4 s1 (.E(adder_5_out), .S(s1_s));
  shifteur4 s2 (.E({adder_3_out[0], adder_3_out_2}), .S(s2_s));
  assign and_1_out = c1_s & 4'b0011;  // AND_Gate and_1, 4 bits wide
  comparator5 c2 (.E(adder_1_out), .S(c2_s));
  Adder #(.width(4)) adder_2 (.a(s2_s), .b({3'b000, E[6]}), .out(A0out), .cin(1'b0));  // open: cout
  shifteur7 s3 (.E(E), .S(Eout));
  Adder #(.width(4)) adder_3 (
    .a(A0), .b(and_1_out), .out({adder_3_out[0], adder_3_out_2}), .cin(1'b0), .cout(adder_3_cout[0]));
  assign and_2_out = 4'b0011 & c2_s;  // AND_Gate and_2, 4 bits wide
  Adder #(.width(4)) adder_4 (.a(s1_s), .b({3'b000, adder_3_out[0]}), .out(A1out), .cin(1'b0));  // open: cout
  Adder #(.width(4)) adder_5 (.a(and_2_out), .b(A1), .out(adder_5_out), .cin(1'b0));  // open: cout

  // Notes on the sheet:
  //   A0'
  //   A1'
  //   A0out
  //   A1out
endmodule

module comparator5 (
  input  [3:0] E,
  output [3:0] S
);

  wire and_1_out, and_2_out;

  and and_1 (and_1_out, E[0], E[2]);
  and and_2 (and_2_out, E[1], E[2]);
  or or_1 (S[3], and_1_out, and_2_out, E[3]);

  assign S[2:0] = {3{S[3]}};
endmodule

module double_dabble (
  input  [6:0] E,
  output [3:0] A0,
  output [3:0] A1
);

  wire [3:0] d1_a0out, d1_a1out, d2_a0out, d2_a1out, d3_a0out, d3_a1out, d4_a0out, d4_a1out, d5_a0out,
       d5_a1out, d6_a0out, d6_a1out;
  wire [6:0] d1_eout, d2_eout, d3_eout, d4_eout, d5_eout, d6_eout;

  double_dabble_1step d1 (.A0(4'b0000), .A1(4'b0000), .E(E), .A0out(d1_a0out), .A1out(d1_a1out), .Eout(d1_eout));
  double_dabble_1step d5 (
    .A0(d4_a0out), .A1(d4_a1out), .E(d4_eout), .A0out(d5_a0out), .A1out(d5_a1out), .Eout(d5_eout));
  double_dabble_1step d2 (
    .A0(d1_a0out), .A1(d1_a1out), .E(d1_eout), .A0out(d2_a0out), .A1out(d2_a1out), .Eout(d2_eout));
  double_dabble_1step d6 (
    .A0(d5_a0out), .A1(d5_a1out), .E(d5_eout), .A0out(d6_a0out), .A1out(d6_a1out), .Eout(d6_eout));
  double_dabble_1step d3 (
    .A0(d2_a0out), .A1(d2_a1out), .E(d2_eout), .A0out(d3_a0out), .A1out(d3_a1out), .Eout(d3_eout));
  double_dabble_1step d7 (.A0(d6_a0out), .A1(d6_a1out), .E(d6_eout), .A0out(A0), .A1out(A1));  // open: Eout
  double_dabble_1step d4 (
    .A0(d3_a0out), .A1(d3_a1out), .E(d3_eout), .A0out(d4_a0out), .A1out(d4_a1out), .Eout(d4_eout));
endmodule

module print_number (
  input  [6:0] E,
  input  [1:0] P,
  output [7:0] S0,
  output [7:0] S1
);

  wire [3:0] dd1_a0, dd1_a1;

  double_dabble dd1 (.E(E), .A0(dd1_a0), .A1(dd1_a1));
  decodeur_7seg_mieux ds1 (.P(P[0]), .E({1'b0, dd1_a0}), .S(S0));
  decodeur_7seg_mieux ds2 (.P(P[1]), .E({1'b0, dd1_a1}), .S(S1));
endmodule

module print_hour (
  input  [6:0] S,
  input  [6:0] M,
  input  [6:0] H,
  output [7:0] S0,
  output [7:0] S1,
  output [7:0] S2,
  output [7:0] S3,
  output [7:0] S4,
  output [7:0] S5
);

  print_number p1 (.E(S), .P(2'b00), .S0(S0), .S1(S1));
  print_number p2 (.E(M), .P(2'b01), .S0(S2), .S1(S3));
  print_number p3 (.E(H), .P(2'b01), .S0(S4), .S1(S5));
  _7_Segment_Display u_7_segment_display_1 (
    .g(S0[6]), .f(S0[5]), .a(S0[0]), .b(S0[1]), .e(S0[4]), .d(S0[3]), .c(S0[2]));  // open: dp
endmodule
